# Fritzing sketch gcGame - Pro Micro Arduboy SH1106 (saved by Fritzing 0.9.3b)
breadboards: 2

parts:
  o2 = Module display OLED SPI 128x64 SH1106 [package=THT]
  S1 = Pushbutton [package="[THT]"]
  S2 = Pushbutton [package="[THT]"]
  S3 = Pushbutton [package="[THT]"]
  S4 = Pushbutton [package="[THT]"]
  S5 = Pushbutton [package="[THT]"]
  Pro_Micro1 = Pro Micro
  S6 = Pushbutton [package="[THT]"]
  S7 = buzzer [part_number=100-SP-X-T1-0-0-B1-M1 package=THT]
  VCC1 = 4 x AAA Battery Mount
  S8 = Toggle Switch [package=THT]

nets:
  VCC: o2.VCC, Pro_Micro1.VCC
  N1: o2.GND, Pro_Micro1.GND#4
  N2: o2.DIN, Pro_Micro1.D16/MOSI
  N3: o2.CLK, Pro_Micro1.D15/SCLK
  N4: o2.D/C, Pro_Micro1.D4
  N5: o2.RES, Pro_Micro1.D6
  N6: S1.Pin_1, S1.Pin_2, S2.Pin_3, S2.Pin_4, S3.Pin_3, S4.Pin_3, S4.Pin_4, S5.Pin_3, S5.Pin_4, Pro_Micro1.GND#23, S6.Pin_3
  N7: S1.Pin_3, S1.Pin_4, Pro_Micro1.D20/A2
  N8: S2.Pin_1, Pro_Micro1.D18/A0
  N9: S3.Pin_1, S3.Pin_2, Pro_Micro1.D21/A3
  N10: S4.Pin_1, S4.Pin_2, Pro_Micro1.D19/A1
  N11: S5.Pin_1, Pro_Micro1.D8
  N12: Pro_Micro1.GND#3, VCC1.-
  N13: Pro_Micro1.D5, S7.2
  N14: Pro_Micro1.D7, S6.Pin_1, S6.Pin_2
  N15: Pro_Micro1.RAW, S8.L1
  N16: VCC1.+, S8.COM

notes:
  gcGame - Pro Micro Arduboy

custom parts:
  Module display OLED SPI 128x64 SH1106: Ecran OLED SPI SH1106 de 128x64
  Pushbutton: A generic pushbutton.
  Pro Micro: The SparkFun Pro Micro is a complete USB-based microcontoller development system, in a very small footprint, capable of implementing many types of projects. All programming can be done via the USB port.
